# Fritzing sketch FinalPCB (saved by Fritzing 0.9.4)
circuit board: 8.99914cm x 6.33507cm
breadboards: 1

parts:
  Accelerometer = Triple Axis Accelerometer Breakout - ADXL345
  LED = LED - 5mm [color="Red (633nm)" package="5 mm [THT]"]
  Transistor = NPN-Transistor [package="TO92 [THT]"]
  R1 = Resistor [tolerance=±5% resistance=220 package=THT]
  R2 = Resistor [tolerance=±5% resistance=2.2k package=THT]
  Sound_sensor = KY-037 High Sensitivity Sound Detection Module [package="Breakout board"]
  Pulse_Oximeter = GY-MAX30102
  Temperature_Sensor = TMP006 Thermopile Sensor
  Raspberry_Pi_3 = Raspberry Pi 3 [part_number=RPI-3-V1.2]
  R4 = Resistor [tolerance=±5% resistance=2k package=THT]
  R3 = Resistor [tolerance=±5% resistance=1k package=THT]
  Extra_Heeader = female pin header, 8 pins [form="♀ (female)"]

nets:
  GND: Accelerometer.GND, Transistor.E, Sound_sensor.G, Pulse_Oximeter.GND, Temperature_Sensor.GND, Raspberry_Pi_3.GND, R4.Pin_0, Extra_Heeader.pin5
  3.3V: Accelerometer.VCC, Pulse_Oximeter.VIN, Temperature_Sensor.VCC, Raspberry_Pi_3.3v3, Raspberry_Pi_3.3V3, Extra_Heeader.pin1
  SDA: Accelerometer.SDA, Pulse_Oximeter.SDA, Temperature_Sensor.SDA, Raspberry_Pi_3.GPIO2, Extra_Heeader.pin2
  SCL: Accelerometer.SCL, Pulse_Oximeter.SCL, Temperature_Sensor.SCL, Raspberry_Pi_3.GPIO3, Extra_Heeader.pin3
  N1: LED.cathode, Transistor.C
  N2: LED.anode, R1.Pin_1
  N3: Transistor.B, R2.Pin_1
  5V: R1.Pin_0, Sound_sensor.+, Raspberry_Pi_3.5V, Extra_Heeader.pin4
  LED: R2.Pin_0, Raspberry_Pi_3.GPIO21
  N4: Sound_sensor.D0, R3.Pin_0
  GPIO 17: Raspberry_Pi_3.GPIO17, Extra_Heeader.pin6
  GPIO 27: Raspberry_Pi_3.GPIO27, Extra_Heeader.pin7
  GPIO 22: Raspberry_Pi_3.GPIO22, Extra_Heeader.pin8
  Sound: Raspberry_Pi_3.GPIO13, R4.Pin_1, R3.Pin_1

notes:
  SDA
  SCL
  3.3V
  5V
  D0
  GND

custom parts:
  KY-037 High Sensitivity Sound Detection Module: KY-037 high sensitivity sound detection module is an analog/digital sensor that uses a condenser microphone to observe changes in environment noise.
  GY-MAX30102: Oximeter module using the MAX30102 chip. You may wish to read (and check your module) this post on power problems with these modules: https://reedpaper.wordpress.com/2018/08/22/pulse-oximeter-max30100-max30102-how-to-fix-wrong-board/ (may not apply as this is a different module!). As usual, if you want the mounting holes in pcb, you need to drag a hole over the pad in silkscreen to actually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
  TMP006 Thermopile Sensor: Unlike all the other temperature sensors we have, this breakout has a really cool IR sensor from TI that can measure the temperature of an object without touching it! Simply point the sensor towards what you want to measure and it will detect the temperature by absorbing IR waves emitted. The embedded thermopile sensor generates a very very small voltage depending on how much IR there is, and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
